# Fritzing sketch hydrophonics shield (saved by Fritzing 0.7.4b)
perfboards: 1

parts:
  IC1 = ULN2003A [package="DIP16 [THT]"]
  Arduino_Ethernet_Shield1 = Arduino Ethernet Shield
  R2 = Resistor [tolerance=±5% resistance=10k package=THT]
  R3 = Resistor [tolerance=±5% resistance=10k package=THT]
  RHT1 = Humidity and Temperature Sensor RHT03
  R1 = Resistor [tolerance=±5% resistance=33 package=THT]
  SCT_013-000 = Inductor [package="400 mil [THT]"]  # not connected
  C1 = Electrolytic Capacitor [capacitance=10µF package="100 mil [THT, electrolytic]"]
  R4 = Resistor [tolerance=±5% resistance=10k package=THT]
  K1 = Relay [part_number=FRS1B-S package=THT]

nets (from the schematic view):
  N1: IC1.In_1, Arduino_Ethernet_Shield1.D5
  N2: IC1.In_2, Arduino_Ethernet_Shield1.SS
  N3: IC1.In_3, Arduino_Ethernet_Shield1.D3
  N4: IC1.In_4, Arduino_Ethernet_Shield1.D2
  N5: IC1.In_5, Arduino_Ethernet_Shield1.D1TX
  N6: IC1.0V, Arduino_Ethernet_Shield1.GND, R3.Pin_1, RHT1.GND_1, C1.-
  +5V: IC1.COM_-_Common, Arduino_Ethernet_Shield1.+5V, R2.Pin_0, RHT1.Vcc, R4.Pin_0, K1.B
  N7: IC1.Out_1, K1.A
  N8: Arduino_Ethernet_Shield1.D0RX, RHT1.Data-signal, R4.Pin_1
  N9: Arduino_Ethernet_Shield1.A0, R1.Pin_1
  N10: R2.Pin_1, R3.Pin_0, R1.Pin_0, C1.+
